# Fritzing sketch nano2nodemcu (saved by Fritzing 0.9.3b)
breadboards: 1

parts:
  Part1 = Arduino Nano (Rev3.0) (ICSP)
  Part2 = SparkFun ESP8266 Thing

nets:
  N1: Part1.D1/TX, Part2.U0RXI
  N2: Part1.D0/RX, Part2.U0TXO
  GND: Part1.GND, Part2.GND
  5V: Part1.5V, Part2.VIN
